// Logisim project 01_rs_latch.circ as structural Verilog
module P1_RS_latch (
  input  R,
  input  S,
  output Q_gate,
  output NQ_gate,
  output Q_vhdl,
  output NQ_vhdl
);

  nor nor_1 (Q_gate, R, NQ_gate);
  nor nor_2 (NQ_gate, Q_gate, S);
  rs_latch_vhdl rs_latch_vhdl_1 (.r(R), .s(S), .q(Q_vhdl), .nq(NQ_vhdl));

  // Notes on the sheet:
  //   R: initial=0x1
endmodule

// VHDL entity rs_latch_vhdl, as the project stores it:
library ieee;
use ieee.std_logic_1164.all;

entity rs_latch_vhdl is
    port (r, s : in std_logic; q, nq : out std_logic);
end entity rs_latch_vhdl;

architecture rtl of rs_latch_vhdl is
begin
    process(r, s)
    begin
        if r = '1' then
            q <= '0';
        elsif s = '1' then
            q <= '1';
        end if;

        if s = '1' then
            nq <= '0';
        elsif r = '1' then
            nq <= '1';
        end if;
    end process;
end architecture rtl;
