// Logisim project 02_d_latch.circ as structural Verilog
module P2_D_latch (
  input  D,
  input  en,
  output Q_gate,
  output NQ_gate,
  output Q_vhdl,
  output NQ_vhdl
);

  wire nand_1_out, nand_2_out, not_1_out;

  not not_1 (not_1_out, D);
  nand nand_1 (nand_1_out, D, en);
  nand nand_2 (nand_2_out, en, not_1_out);
  nand nand_3 (Q_gate, nand_1_out, NQ_gate);
  nand nand_4 (NQ_gate, Q_gate, nand_2_out);
  d_latch_vhdl d_latch_vhdl_1 (.d(D), .en(en), .q(Q_vhdl), .nq(NQ_vhdl));

  // Notes on the sheet:
  //   en: initial=0x1
endmodule

// VHDL entity d_latch_vhdl, as the project stores it:
library ieee;
use ieee.std_logic_1164.all;

entity d_latch_vhdl is
    port (d, en : in std_logic; q, nq : out std_logic);
end entity d_latch_vhdl;

architecture rtl of d_latch_vhdl is
    signal q_i : std_logic;
begin
    process(d, en)
    begin
        if en = '1' then
            q_i <= d;
        end if;
    end process;
    q <= q_i;
    nq <= not q_i;
end architecture rtl;
