// Logisim project 03_d_flipflop.circ as structural Verilog
module P3_D_flipflop (
  input  D,
  input  CLK,
  output Q_gate,
  output NQ_gate,
  output Q_vhdl,
  output NQ_vhdl
);

  wire nand_1_out, nand_2_out, nand_3_out, nand_4_out, nand_5_out, nand_6_out, not_1_out, not_2_out,
       not_3_out, not_4_out;

  not not_1 (not_1_out, CLK);
  not not_2 (not_2_out, D);
  nand nand_1 (nand_1_out, D, not_1_out);
  nand nand_2 (nand_2_out, not_1_out, not_2_out);
  not not_3 (not_3_out, not_1_out);
  nand nand_3 (nand_3_out, nand_1_out, nand_4_out);
  nand nand_4 (nand_4_out, nand_3_out, nand_2_out);
  not not_4 (not_4_out, nand_3_out);
  nand nand_5 (nand_5_out, nand_3_out, not_3_out);
  nand nand_6 (nand_6_out, not_3_out, not_4_out);
  d_flipflop_vhdl d_flipflop_vhdl_1 (.d(D), .clk(CLK), .q(Q_vhdl), .nq(NQ_vhdl));
  nand nand_7 (Q_gate, nand_5_out, NQ_gate);
  nand nand_8 (NQ_gate, Q_gate, nand_6_out);
endmodule

// VHDL entity d_flipflop_vhdl, as the project stores it:
library ieee;
use ieee.std_logic_1164.all;

entity d_flipflop_vhdl is
    port (d, clk : in std_logic; q, nq : out std_logic);
end entity d_flipflop_vhdl;

architecture rtl of d_flipflop_vhdl is
    signal q_i : std_logic;
begin
    process(clk)
    begin
        if rising_edge(clk) then
            q_i <= d;
        end if;
    end process;
    q <= q_i;
    nq <= not q_i;
end architecture rtl;
