// Logisim project 04_jk_flipflop.circ as structural Verilog
module P4_JK_flipflop (
  input  J,
  input  K,
  input  CLK,
  input  CLR_N,
  output Q_gate,
  output NQ_gate,
  output Q_vhdl,
  output NQ_vhdl
);

  wire nand_1_out, nand_2_out, nand_3_out, nand_4_out, nand_5_out, nand_6_out, nand_7_out, nand_8_out,
       nand_9_out, nand_10_out, nand_11_out, nand_12_out, nand_13_out, nand_14_out, nand_15_out, nand_16_out;

  nand nand_1 (nand_1_out, K, K);
  nand nand_2 (nand_2_out, CLK, CLK);
  nand nand_3 (nand_3_out, J, NQ_gate);
  nand nand_4 (nand_4_out, nand_1_out, Q_gate);
  nand nand_5 (nand_5_out, nand_2_out, CLR_N);
  nand nand_6 (nand_6_out, CLK, CLR_N);
  nand nand_7 (nand_7_out, nand_3_out, nand_4_out);
  nand nand_8 (nand_8_out, nand_5_out, nand_5_out);
  nand nand_9 (nand_9_out, nand_6_out, nand_6_out);
  nand nand_10 (nand_10_out, nand_7_out, nand_7_out);
  jk_flipflop_vhdl jk_flipflop_vhdl_1 (.j(J), .k(K), .clk(CLK), .clr_n(CLR_N), .q(Q_vhdl), .nq(NQ_vhdl));
  nand nand_11 (nand_11_out, nand_7_out, nand_8_out);
  nand nand_12 (nand_12_out, nand_10_out, nand_8_out);
  nand nand_13 (nand_13_out, nand_11_out, nand_14_out);
  nand nand_14 (nand_14_out, nand_13_out, nand_12_out, CLR_N);
  nand nand_15 (nand_15_out, nand_13_out, nand_9_out);
  nand nand_16 (nand_16_out, nand_14_out, nand_9_out);
  nand nand_17 (Q_gate, nand_15_out, NQ_gate);
  nand nand_18 (NQ_gate, Q_gate, nand_16_out, CLR_N);

  // Notes on the sheet:
  //   K: initial=0x1
endmodule

// VHDL entity jk_flipflop_vhdl, as the project stores it:
library ieee;
use ieee.std_logic_1164.all;

entity jk_flipflop_vhdl is
    port (j, k, clk, clr_n : in std_logic; q, nq : out std_logic);
end entity jk_flipflop_vhdl;

architecture rtl of jk_flipflop_vhdl is
    signal q_i : std_logic;
begin
    process(clk, clr_n)
    begin
        if clr_n = '0' then
            q_i <= '0';
        elsif rising_edge(clk) then
            if j = '0' and k = '1' then
                q_i <= '0';
            elsif j = '1' and k = '0' then
                q_i <= '1';
            elsif j = '1' and k = '1' then
                q_i <= not q_i;
            end if;
        end if;
    end process;
    q <= q_i;
    nq <= not q_i;
end architecture rtl;
