// Logisim project 05_dff_async.circ as structural Verilog
module P5_DFF_async (
  input  D,
  input  CLK,
  input  SET,
  input  CLR,
  output Q_gate,
  output NQ_gate,
  output Q_vhdl,
  output NQ_vhdl
);

  wire and_1_out, and_2_out, nand_1_out, nand_2_out, nand_3_out, nand_4_out, nand_5_out, nand_6_out,
       nand_7_out, nor_1_out, not_1_out, not_2_out, not_3_out, not_4_out;

  not not_1 (not_1_out, CLK);
  not not_2 (not_2_out, CLR);
  and and_1 (and_1_out, not_1_out, nor_1_out);
  nor nor_1 (nor_1_out, SET, CLR);
  not not_3 (not_3_out, D);
  nand nand_1 (nand_1_out, D, and_1_out);
  nand nand_2 (nand_2_out, not_3_out, and_1_out);
  nand nand_3 (nand_3_out, SET, not_2_out);
  nand nand_4 (nand_4_out, nand_1_out, nand_3_out, nand_5_out);
  nand nand_5 (nand_5_out, nand_4_out, not_2_out, nand_2_out);
  dff_async_vhdl dff_async_vhdl_1 (.d(D), .clk(CLK), .set(SET), .clr(CLR), .q(Q_vhdl), .nq(NQ_vhdl));
  and and_2 (and_2_out, CLK, nor_1_out);
  not not_4 (not_4_out, nand_4_out);
  nand nand_6 (nand_6_out, nand_4_out, and_2_out);
  nand nand_7 (nand_7_out, not_4_out, and_2_out);
  nand nand_8 (Q_gate, nand_6_out, nand_3_out, NQ_gate);
  nand nand_9 (NQ_gate, Q_gate, not_2_out, nand_7_out);

  // Notes on the sheet:
  //   CLR: initial=0x1
endmodule

// VHDL entity dff_async_vhdl, as the project stores it:
library ieee;
use ieee.std_logic_1164.all;

entity dff_async_vhdl is
    port (d, clk, set, clr : in std_logic; q, nq : out std_logic);
end entity dff_async_vhdl;

architecture rtl of dff_async_vhdl is
    signal q_i : std_logic;
begin
    process(clk, set, clr)
    begin
        if clr = '1' then
            q_i <= '0';
        elsif set = '1' then
            q_i <= '1';
        elsif rising_edge(clk) then
            q_i <= d;
        end if;
    end process;
    q <= q_i;
    nq <= not q_i;
end architecture rtl;
