// Logisim project VHDL3_all.circ as structural Verilog
module P1_RS_latch (
  input  R,
  input  S,
  output Q_gate,
  output NQ_gate,
  output Q_vhdl,
  output NQ_vhdl
);

  nor nor_1 (Q_gate, R, NQ_gate);
  nor nor_2 (NQ_gate, Q_gate, S);
  rs_latch_vhdl rs_latch_vhdl_1 (.r(R), .s(S), .q(Q_vhdl), .nq(NQ_vhdl));

  // Notes on the sheet:
  //   R: initial=0x1
endmodule

module P2_D_latch (
  input  D,
  input  en,
  output Q_gate,
  output NQ_gate,
  output Q_vhdl,
  output NQ_vhdl
);

  wire nand_1_out, nand_2_out, not_1_out;

  not not_1 (not_1_out, D);
  nand nand_1 (nand_1_out, D, en);
  nand nand_2 (nand_2_out, en, not_1_out);
  nand nand_3 (Q_gate, nand_1_out, NQ_gate);
  nand nand_4 (NQ_gate, Q_gate, nand_2_out);
  d_latch_vhdl d_latch_vhdl_1 (.d(D), .en(en), .q(Q_vhdl), .nq(NQ_vhdl));

  // Notes on the sheet:
  //   en: initial=0x1
endmodule

module P3_D_flipflop (
  input  D,
  input  CLK,
  output Q_gate,
  output NQ_gate,
  output Q_vhdl,
  output NQ_vhdl
);

  wire nand_1_out, nand_2_out, nand_3_out, nand_4_out, nand_5_out, nand_6_out, not_1_out, not_2_out,
       not_3_out, not_4_out;

  not not_1 (not_1_out, CLK);
  not not_2 (not_2_out, D);
  nand nand_1 (nand_1_out, D, not_1_out);
  nand nand_2 (nand_2_out, not_1_out, not_2_out);
  not not_3 (not_3_out, not_1_out);
  nand nand_3 (nand_3_out, nand_1_out, nand_4_out);
  nand nand_4 (nand_4_out, nand_3_out, nand_2_out);
  not not_4 (not_4_out, nand_3_out);
  nand nand_5 (nand_5_out, nand_3_out, not_3_out);
  nand nand_6 (nand_6_out, not_3_out, not_4_out);
  d_flipflop_vhdl d_flipflop_vhdl_1 (.d(D), .clk(CLK), .q(Q_vhdl), .nq(NQ_vhdl));
  nand nand_7 (Q_gate, nand_5_out, NQ_gate);
  nand nand_8 (NQ_gate, Q_gate, nand_6_out);
endmodule

module P4_JK_flipflop (
  input  J,
  input  K,
  input  CLK,
  input  CLR_N,
  output Q_gate,
  output NQ_gate,
  output Q_vhdl,
  output NQ_vhdl
);

  wire nand_1_out, nand_2_out, nand_3_out, nand_4_out, nand_5_out, nand_6_out, nand_7_out, nand_8_out,
       nand_9_out, nand_10_out, nand_11_out, nand_12_out, nand_13_out, nand_14_out, nand_15_out, nand_16_out;

  nand nand_1 (nand_1_out, K, K);
  nand nand_2 (nand_2_out, CLK, CLK);
  nand nand_3 (nand_3_out, J, NQ_gate);
  nand nand_4 (nand_4_out, nand_1_out, Q_gate);
  nand nand_5 (nand_5_out, nand_2_out, CLR_N);
  nand nand_6 (nand_6_out, CLK, CLR_N);
  nand nand_7 (nand_7_out, nand_3_out, nand_4_out);
  nand nand_8 (nand_8_out, nand_5_out, nand_5_out);
  nand nand_9 (nand_9_out, nand_6_out, nand_6_out);
  nand nand_10 (nand_10_out, nand_7_out, nand_7_out);
  jk_flipflop_vhdl jk_flipflop_vhdl_1 (.j(J), .k(K), .clk(CLK), .clr_n(CLR_N), .q(Q_vhdl), .nq(NQ_vhdl));
  nand nand_11 (nand_11_out, nand_7_out, nand_8_out);
  nand nand_12 (nand_12_out, nand_10_out, nand_8_out);
  nand nand_13 (nand_13_out, nand_11_out, nand_14_out);
  nand nand_14 (nand_14_out, nand_13_out, nand_12_out, CLR_N);
  nand nand_15 (nand_15_out, nand_13_out, nand_9_out);
  nand nand_16 (nand_16_out, nand_14_out, nand_9_out);
  nand nand_17 (Q_gate, nand_15_out, NQ_gate);
  nand nand_18 (NQ_gate, Q_gate, nand_16_out, CLR_N);

  // Notes on the sheet:
  //   K: initial=0x1
endmodule

module P5_DFF_async (
  input  D,
  input  CLK,
  input  SET,
  input  CLR,
  output Q_gate,
  output NQ_gate,
  output Q_vhdl,
  output NQ_vhdl
);

  wire and_1_out, and_2_out, nand_1_out, nand_2_out, nand_3_out, nand_4_out, nand_5_out, nand_6_out,
       nand_7_out, nor_1_out, not_1_out, not_2_out, not_3_out, not_4_out;

  not not_1 (not_1_out, CLK);
  not not_2 (not_2_out, CLR);
  and and_1 (and_1_out, not_1_out, nor_1_out);
  nor nor_1 (nor_1_out, SET, CLR);
  not not_3 (not_3_out, D);
  nand nand_1 (nand_1_out, D, and_1_out);
  nand nand_2 (nand_2_out, not_3_out, and_1_out);
  nand nand_3 (nand_3_out, SET, not_2_out);
  nand nand_4 (nand_4_out, nand_1_out, nand_3_out, nand_5_out);
  nand nand_5 (nand_5_out, nand_4_out, not_2_out, nand_2_out);
  dff_async_vhdl dff_async_vhdl_1 (.d(D), .clk(CLK), .set(SET), .clr(CLR), .q(Q_vhdl), .nq(NQ_vhdl));
  and and_2 (and_2_out, CLK, nor_1_out);
  not not_4 (not_4_out, nand_4_out);
  nand nand_6 (nand_6_out, nand_4_out, and_2_out);
  nand nand_7 (nand_7_out, not_4_out, and_2_out);
  nand nand_8 (Q_gate, nand_6_out, nand_3_out, NQ_gate);
  nand nand_9 (NQ_gate, Q_gate, not_2_out, nand_7_out);

  // Notes on the sheet:
  //   CLR: initial=0x1
endmodule

// VHDL entity rs_latch_vhdl, as the project stores it:
library ieee;
use ieee.std_logic_1164.all;

entity rs_latch_vhdl is
    port (r, s : in std_logic; q, nq : out std_logic);
end entity rs_latch_vhdl;

architecture rtl of rs_latch_vhdl is
begin
    process(r, s)
    begin
        if r = '1' then
            q <= '0';
        elsif s = '1' then
            q <= '1';
        end if;

        if s = '1' then
            nq <= '0';
        elsif r = '1' then
            nq <= '1';
        end if;
    end process;
end architecture rtl;

// VHDL entity d_latch_vhdl, as the project stores it:
library ieee;
use ieee.std_logic_1164.all;

entity d_latch_vhdl is
    port (d, en : in std_logic; q, nq : out std_logic);
end entity d_latch_vhdl;

architecture rtl of d_latch_vhdl is
    signal q_i : std_logic;
begin
    process(d, en)
    begin
        if en = '1' then
            q_i <= d;
        end if;
    end process;
    q <= q_i;
    nq <= not q_i;
end architecture rtl;

// VHDL entity d_flipflop_vhdl, as the project stores it:
library ieee;
use ieee.std_logic_1164.all;

entity d_flipflop_vhdl is
    port (d, clk : in std_logic; q, nq : out std_logic);
end entity d_flipflop_vhdl;

architecture rtl of d_flipflop_vhdl is
    signal q_i : std_logic;
begin
    process(clk)
    begin
        if rising_edge(clk) then
            q_i <= d;
        end if;
    end process;
    q <= q_i;
    nq <= not q_i;
end architecture rtl;

// VHDL entity jk_flipflop_vhdl, as the project stores it:
library ieee;
use ieee.std_logic_1164.all;

entity jk_flipflop_vhdl is
    port (j, k, clk, clr_n : in std_logic; q, nq : out std_logic);
end entity jk_flipflop_vhdl;

architecture rtl of jk_flipflop_vhdl is
    signal q_i : std_logic;
begin
    process(clk, clr_n)
    begin
        if clr_n = '0' then
            q_i <= '0';
        elsif rising_edge(clk) then
            if j = '0' and k = '1' then
                q_i <= '0';
            elsif j = '1' and k = '0' then
                q_i <= '1';
            elsif j = '1' and k = '1' then
                q_i <= not q_i;
            end if;
        end if;
    end process;
    q <= q_i;
    nq <= not q_i;
end architecture rtl;

// VHDL entity dff_async_vhdl, as the project stores it:
library ieee;
use ieee.std_logic_1164.all;

entity dff_async_vhdl is
    port (d, clk, set, clr : in std_logic; q, nq : out std_logic);
end entity dff_async_vhdl;

architecture rtl of dff_async_vhdl is
    signal q_i : std_logic;
begin
    process(clk, set, clr)
    begin
        if clr = '1' then
            q_i <= '0';
        elsif set = '1' then
            q_i <= '1';
        elsif rising_edge(clk) then
            q_i <= d;
        end if;
    end process;
    q <= q_i;
    nq <= not q_i;
end architecture rtl;
